// Logisim project Learn.circ as structural Verilog: 5 circuits, main circuit ALU
module ALU (
  input  S,
  input  [7:0] X,
  input  [7:0] Y,
  output [7:0] result,
  output equal
);

  wire [7:0] adder_1_out, adder_2_out, negator_1_out;

  Negator negator_1 (.in(Y), .out(negator_1_out));
  Comparator comparator_1 (.a(Y), .b(X), .eq(equal));  // open: gt, lt
  Adder adder_1 (.a(X), .b(Y), .out(adder_1_out));  // open: cin, cout
  Adder adder_2 (.a(X), .b(negator_1_out), .out(adder_2_out));  // open: cin, cout
  Multiplexer #(.width(8), .enable("false")) multiplexer_1 (
    .in0(adder_1_out), .in1(adder_2_out), .out(result), .sel(S));

  // Notes on the sheet:
  //   符号加
  //   符号减
endmodule

module RegFile (
  input  [7:0] din,
  input  we,
  input  clk,
  input  [1:0] R1,
  input  [1:0] R2,
  input  [1:0] Wb,
  output [7:0] R1_2,
  output [7:0] R2_2,
  output [7:0] Seg
);

  wire decoder_1_out0, decoder_1_out1, decoder_1_out2, decoder_1_out3;
  wire [7:0] register_1_q, register_2_q, register_3_q;

  Decoder #(.select(2), .disabled(0)) decoder_1 (
    .out0(decoder_1_out0), .out1(decoder_1_out1), .out2(decoder_1_out2), .out3(decoder_1_out3), .sel(Wb),
    .en(we));
  Register #(.Select("low")) register_1 (.D(din), .en(decoder_1_out0), .Q(register_1_q), .clk(clk), .clr(1'b1));
  Register #(.Select("low")) register_2 (.D(din), .en(decoder_1_out1), .Q(register_2_q), .clk(clk));  // open: clr
  Register #(.Select("low")) register_3 (.D(din), .en(decoder_1_out2), .Q(register_3_q), .clk(clk));  // open: clr
  Register #(.Select("low")) register_4 (.D(din), .en(decoder_1_out3), .Q(Seg), .clk(clk));  // open: clr
  Multiplexer #(.select(2), .width(8), .enable("false")) multiplexer_1 (
    .in0(register_1_q), .in1(register_2_q), .in2(register_3_q), .in3(Seg), .out(R1_2), .sel(R1));
  Multiplexer #(.select(2), .width(8), .enable("false")) multiplexer_2 (
    .in0(register_1_q), .in1(register_2_q), .in2(register_3_q), .in3(Seg), .out(R2_2), .sel(R2));

  // Notes on the sheet:
  //   数据写回寄存器编号
  //   以3号寄存器当作基址寄存器
endmodule

module Pic (
  input  [31:0] din,
  input  clk,
  input  ready,
  input  restart,
  output [31:0] out_5,
  output [31:0] out_6,
  output [31:0] out_7,
  output [31:0] out_8,
  output [31:0] out_9,
  output [31:0] out_10,
  output [31:0] out_11,
  output [31:0] out_12,
  output [31:0] out_13,
  output [31:0] out_14,
  output [31:0] out_15,
  output [31:0] out_16,
  output [31:0] out_17,
  output [31:0] out_18,
  output [31:0] out_19,
  output [31:0] out_20,
  output [31:0] out_21,
  output [31:0] out_22,
  output [31:0] out_23,
  output [31:0] out_24,
  output [31:0] out_25,
  output [31:0] out_26,
  output [31:0] out_27,
  output [31:0] out_28,
  output [31:0] out_29,
  output [31:0] out_30,
  output [31:0] out_31,
  output [31:0] out_32,
  output [31:0] out_33,
  output [31:0] out_34,
  output [31:0] out_35,
  output [31:0] out_36
);

  wire counter_1_carry, i1, i2, i3, i4, i5, i6, i7, i8, i9, i10, i11, i12, i13, i14, i15, i16, i17, i18, i19,
       i20, i21, i22, i23, i24, i25, i26, i27, i28, i29, i30, i31, i32, \input ;
  wire [4:0] counter_1_q;
  wire [31:0] o1, o2, o3, o4, o5, o6, o7, o8, o9, o10, o11, o12, o13, o14, o15, o16, o17, o18, o19, o20, o21,
       o22, o23, o24, o25, o26, o27, o28, o29, o30, o31, o32;

  Register #(.width(32), .Select("low")) register_1 (.D(o1), .Q(out_5), .clk(\input ));  // open: en, clr
  Register #(.width(32), .Select("low")) register_2 (.D(o9), .Q(out_13), .clk(\input ));  // open: en, clr
  Register #(.width(32), .Select("low")) register_3 (.D(o17), .Q(out_21), .clk(\input ));  // open: en, clr
  Register #(.width(32), .Select("low")) register_4 (.D(o25), .Q(out_29), .clk(\input ));  // open: en, clr
  Decoder #(.select(5), .disabled(0)) decoder_1 (
    .out0(i1), .out1(i2), .out2(i3), .out3(i4), .out4(i5), .out5(i6), .out6(i7), .out7(i8), .out8(i9),
    .out9(i10), .out10(i11), .out11(i12), .out12(i13), .out13(i14), .out14(i15), .out15(i16), .out16(i17),
    .out17(i18), .out18(i19), .out19(i20), .out20(i21), .out21(i22), .out22(i23), .out23(i24), .out24(i25),
    .out25(i26), .out26(i27), .out27(i28), .out28(i29), .out29(i30), .out30(i31), .out31(i32),
    .sel(counter_1_q), .en(ready));
  Counter #(.width(5), .max('h1f)) counter_1 (
    .load(restart), .D({5{1'b0}}), .count(ready), .Q(counter_1_q), .carry(counter_1_carry), .clk(clk));  // open: clr, preset, down
  not not_1 (\input , counter_1_carry);
  Register #(.width(32), .Select("low")) register_5 (.D(o2), .Q(out_6), .clk(\input ));  // open: en, clr
  Register #(.width(32), .Select("low")) register_6 (.D(o10), .Q(out_14), .clk(\input ));  // open: en, clr
  Register #(.width(32), .Select("low")) register_7 (.D(o18), .Q(out_22), .clk(\input ));  // open: en, clr
  Register #(.width(32), .Select("low")) register_8 (.D(o26), .Q(out_30), .clk(\input ));  // open: en, clr
  Register #(.width(32), .Select("low")) register_9 (.D(o3), .Q(out_7), .clk(\input ));  // open: en, clr
  Register #(.width(32), .Select("low")) register_10 (.D(o11), .Q(out_15), .clk(\input ));  // open: en, clr
  Register #(.width(32), .Select("low")) register_11 (.D(o19), .Q(out_23), .clk(\input ));  // open: en, clr
  Register #(.width(32), .Select("low")) register_12 (.D(o27), .Q(out_31), .clk(\input ));  // open: en, clr
  Register #(.width(32), .Select("low")) register_13 (.D(din), .en(i1), .Q(o1), .clk(clk));  // open: clr
  Register #(.width(32), .Select("low")) register_14 (.D(din), .en(i9), .Q(o9), .clk(clk));  // open: clr
  Register #(.width(32), .Select("low")) register_15 (.D(din), .en(i17), .Q(o17), .clk(clk));  // open: clr
  Register #(.width(32), .Select("low")) register_16 (.D(din), .en(i25), .Q(o25), .clk(clk));  // open: clr
  Register #(.width(32), .Select("low")) register_17 (.D(din), .en(i2), .Q(o2), .clk(clk));  // open: clr
  Register #(.width(32), .Select("low")) register_18 (.D(din), .en(i10), .Q(o10), .clk(clk));  // open: clr
  Register #(.width(32), .Select("low")) register_19 (.D(din), .en(i18), .Q(o18), .clk(clk));  // open: clr
  Register #(.width(32), .Select("low")) register_20 (.D(din), .en(i26), .Q(o26), .clk(clk));  // open: clr
  Register #(.width(32), .Select("low")) register_21 (.D(o4), .Q(out_8), .clk(\input ));  // open: en, clr
  Register #(.width(32), .Select("low")) register_22 (.D(o12), .Q(out_16), .clk(\input ));  // open: en, clr
  Register #(.width(32), .Select("low")) register_23 (.D(o20), .Q(out_24), .clk(\input ));  // open: en, clr
  Register #(.width(32), .Select("low")) register_24 (.D(o28), .Q(out_32), .clk(\input ));  // open: en, clr
  Register #(.width(32), .Select("low")) register_25 (.D(din), .en(i3), .Q(o3), .clk(clk));  // open: clr
  Register #(.width(32), .Select("low")) register_26 (.D(din), .en(i11), .Q(o11), .clk(clk));  // open: clr
  Register #(.width(32), .Select("low")) register_27 (.D(din), .en(i19), .Q(o19), .clk(clk));  // open: clr
  Register #(.width(32), .Select("low")) register_28 (.D(din), .en(i27), .Q(o27), .clk(clk));  // open: clr
  Register #(.width(32), .Select("low")) register_29 (.D(din), .en(i4), .Q(o4), .clk(clk));  // open: clr
  Register #(.width(32), .Select("low")) register_30 (.D(din), .en(i12), .Q(o12), .clk(clk));  // open: clr
  Register #(.width(32), .Select("low")) register_31 (.D(din), .en(i20), .Q(o20), .clk(clk));  // open: clr
  Register #(.width(32), .Select("low")) register_32 (.D(din), .en(i28), .Q(o28), .clk(clk));  // open: clr
  Register #(.width(32), .Select("low")) register_33 (.D(din), .en(i5), .Q(o5), .clk(clk));  // open: clr
  Register #(.width(32), .Select("low")) register_34 (.D(din), .en(i13), .Q(o13), .clk(clk));  // open: clr
  Register #(.width(32), .Select("low")) register_35 (.D(din), .en(i21), .Q(o21), .clk(clk));  // open: clr
  Register #(.width(32), .Select("low")) register_36 (.D(din), .en(i29), .Q(o29), .clk(clk));  // open: clr
  Register #(.width(32), .Select("low")) register_37 (.D(o5), .Q(out_9), .clk(\input ));  // open: en, clr
  Register #(.width(32), .Select("low")) register_38 (.D(o13), .Q(out_17), .clk(\input ));  // open: en, clr
  Register #(.width(32), .Select("low")) register_39 (.D(o21), .Q(out_25), .clk(\input ));  // open: en, clr
  Register #(.width(32), .Select("low")) register_40 (.D(o29), .Q(out_33), .clk(\input ));  // open: en, clr
  Register #(.width(32), .Select("low")) register_41 (.D(din), .en(i6), .Q(o6), .clk(clk));  // open: clr
  Register #(.width(32), .Select("low")) register_42 (.D(din), .en(i14), .Q(o14), .clk(clk));  // open: clr
  Register #(.width(32), .Select("low")) register_43 (.D(din), .en(i22), .Q(o22), .clk(clk));  // open: clr
  Register #(.width(32), .Select("low")) register_44 (.D(din), .en(i30), .Q(o30), .clk(clk));  // open: clr
  Register #(.width(32), .Select("low")) register_45 (.D(din), .en(i7), .Q(o7), .clk(clk));  // open: clr
  Register #(.width(32), .Select("low")) register_46 (.D(din), .en(i15), .Q(o15), .clk(clk));  // open: clr
  Register #(.width(32), .Select("low")) register_47 (.D(din), .en(i23), .Q(o23), .clk(clk));  // open: clr
  Register #(.width(32), .Select("low")) register_48 (.D(din), .en(i31), .Q(o31), .clk(clk));  // open: clr
  Register #(.width(32), .Select("low")) register_49 (.D(o6), .Q(out_10), .clk(\input ));  // open: en, clr
  Register #(.width(32), .Select("low")) register_50 (.D(o14), .Q(out_18), .clk(\input ));  // open: en, clr
  Register #(.width(32), .Select("low")) register_51 (.D(o22), .Q(out_26), .clk(\input ));  // open: en, clr
  Register #(.width(32), .Select("low")) register_52 (.D(o30), .Q(out_34), .clk(\input ));  // open: en, clr
  Register #(.width(32), .Select("low")) register_53 (.D(din), .en(i8), .Q(o8), .clk(clk));  // open: clr
  Register #(.width(32), .Select("low")) register_54 (.D(din), .en(i16), .Q(o16), .clk(clk));  // open: clr
  Register #(.width(32), .Select("low")) register_55 (.D(din), .en(i24), .Q(o24), .clk(clk));  // open: clr
  Register #(.width(32), .Select("low")) register_56 (.D(din), .en(i32), .Q(o32), .clk(clk));  // open: clr
  Register #(.width(32), .Select("low")) register_57 (.D(o7), .Q(out_11), .clk(\input ));  // open: en, clr
  Register #(.width(32), .Select("low")) register_58 (.D(o15), .Q(out_19), .clk(\input ));  // open: en, clr
  Register #(.width(32), .Select("low")) register_59 (.D(o23), .Q(out_27), .clk(\input ));  // open: en, clr
  Register #(.width(32), .Select("low")) register_60 (.D(o31), .Q(out_35), .clk(\input ));  // open: en, clr
  Register #(.width(32), .Select("low")) register_61 (.D(o8), .Q(out_12), .clk(\input ));  // open: en, clr
  Register #(.width(32), .Select("low")) register_62 (.D(o16), .Q(out_20), .clk(\input ));  // open: en, clr
  Register #(.width(32), .Select("low")) register_63 (.D(o24), .Q(out_28), .clk(\input ));  // open: en, clr
  Register #(.width(32), .Select("low")) register_64 (.D(o32), .Q(out_36), .clk(\input ));  // open: en, clr
endmodule

module Main (
);

  wire alu_1_equal, clock_1_out, controller_1_alu_operation, controller_1_pc_in, controller_1_ready,
       controller_1_regfile_we, controller_1_update_inst;
  wire [1:0] controller_1_src_y;
  wire [7:0] alu_1_result, Imme_q, Inst_q, inst_sram_data, multiplexer_1_out, PC_q, regfile_1_r1_2,
       regfile_1_r2_2, regfile_1_seg;
  wire [31:0] data_sram_data, Pic_out_5, Pic_out_6, Pic_out_7, Pic_out_8, Pic_out_9, Pic_out_10, Pic_out_11,
       Pic_out_12, Pic_out_13, Pic_out_14, Pic_out_15, Pic_out_16, Pic_out_17, Pic_out_18, Pic_out_19,
       Pic_out_20, Pic_out_21, Pic_out_22, Pic_out_23, Pic_out_24, Pic_out_25, Pic_out_26, Pic_out_27,
       Pic_out_28, Pic_out_29, Pic_out_30, Pic_out_31, Pic_out_32, Pic_out_33, Pic_out_34, Pic_out_35,
       Pic_out_36;

  Controller controller_1 (
    .clk(clock_1_out), .Op(Inst_q[7:5]), .Func(Inst_q[0]), .Equal(alu_1_equal), .Pc_in(controller_1_pc_in),
    .update_inst(controller_1_update_inst), .RegFile_we(controller_1_regfile_we), .src_Y(controller_1_src_y),
    .ALU_operation(controller_1_alu_operation), .ready(controller_1_ready));
  Clock clock_1 (.out(clock_1_out));
  Counter PC (
    .load(controller_1_pc_in), .D(Imme_q), .Q(PC_q), .clk(clock_1_out));  // open: count, carry, clr, preset, down
  RAM #(.Select("low")) inst_sram (.addr(PC_q), .data(inst_sram_data), .clk(clock_1_out));  // open: sel, ld, clr
  Register #(.Select("low")) Inst (
    .D(inst_sram_data), .en(controller_1_update_inst), .Q(Inst_q), .clk(clock_1_out));  // open: clr
  Register #(.Select("low")) Imme (.D(inst_sram_data), .Q(Imme_q), .clk(clock_1_out));  // open: en, clr
  RegFile regfile_1 (
    .din(alu_1_result), .we(controller_1_regfile_we), .clk(clock_1_out), .R1(Inst_q[4:3]), .R2(Inst_q[2:1]),
    .R1_2(regfile_1_r1_2), .R2_2(regfile_1_r2_2), .Wb(Inst_q[4:3]), .Seg(regfile_1_seg));
  ALU alu_1 (
    .result(alu_1_result), .equal(alu_1_equal), .X(regfile_1_r1_2), .Y(multiplexer_1_out),
    .S(controller_1_alu_operation));
  Multiplexer #(.select(2), .width(8), .enable("false")) multiplexer_1 (
    .in0(regfile_1_r2_2), .in1(Imme_q), .in3(8'h1), .out(multiplexer_1_out), .sel(controller_1_src_y));  // open: in2
  RAM #(.addrWidth(16), .dataWidth(32), .Select("low")) data_sram (
    .addr({regfile_1_seg, alu_1_result}), .data(data_sram_data), .clk(clock_1_out));  // open: sel, ld, clr
  DotMatrix #(.inputtype("row"), .matrixcols(32), .matrixrows(32)) dotmatrix_1 (
    .row0(Pic_out_5), .row1(Pic_out_6), .row2(Pic_out_7), .row3(Pic_out_8), .row4(Pic_out_9),
    .row5(Pic_out_10), .row6(Pic_out_11), .row7(Pic_out_12), .row8(Pic_out_13), .row9(Pic_out_14),
    .row10(Pic_out_15), .row11(Pic_out_16), .row12(Pic_out_17), .row13(Pic_out_18), .row14(Pic_out_19),
    .row15(Pic_out_20), .row16(Pic_out_21), .row17(Pic_out_22), .row18(Pic_out_23), .row19(Pic_out_24),
    .row20(Pic_out_25), .row21(Pic_out_26), .row22(Pic_out_27), .row23(Pic_out_28), .row24(Pic_out_29),
    .row25(Pic_out_30), .row26(Pic_out_31), .row27(Pic_out_32), .row28(Pic_out_33), .row29(Pic_out_34),
    .row30(Pic_out_35), .row31(Pic_out_36));
  Pic Pic (
    .din(data_sram_data), .clk(clock_1_out), .out_5(Pic_out_5), .out_6(Pic_out_6), .out_7(Pic_out_7),
    .out_8(Pic_out_8), .out_9(Pic_out_9), .out_10(Pic_out_10), .out_11(Pic_out_11), .out_12(Pic_out_12),
    .out_13(Pic_out_13), .out_14(Pic_out_14), .out_15(Pic_out_15), .out_16(Pic_out_16), .out_17(Pic_out_17),
    .out_18(Pic_out_18), .out_19(Pic_out_19), .out_20(Pic_out_20), .out_21(Pic_out_21), .out_22(Pic_out_22),
    .out_23(Pic_out_23), .out_24(Pic_out_24), .out_25(Pic_out_25), .out_26(Pic_out_26), .out_27(Pic_out_27),
    .out_28(Pic_out_28), .out_29(Pic_out_29), .out_30(Pic_out_30), .out_31(Pic_out_31), .out_32(Pic_out_32),
    .out_33(Pic_out_33), .out_34(Pic_out_34), .out_35(Pic_out_35), .out_36(Pic_out_36),
    .ready(controller_1_ready));  // open: restart

  // Notes on the sheet:
  //   Func
  //   Op
  //   Rt
  //   Rs
  //   Imme
endmodule

module Controller (
  input  clk,
  input  [2:0] Op,
  input  Func,
  input  Equal,
  output Pc_in,
  output update_inst,
  output RegFile_we,
  output [1:0] src_Y,
  output ALU_operation,
  output ready
);

  wire addi_1_out, addi_2_out, and_1_out, and_2_out, and_3_out, and_4_out, Beq_2_out, Bnq_2_out,
       comparator_1_eq, comparator_2_eq, comparator_2_gt, comparator_3_eq, comparator_4_eq, comparator_5_eq,
       comparator_6_eq, comparator_7_eq, comparator_8_eq, comparator_9_eq, jmp_out, not_1_out, not_2_out,
       not_3_out, or_6_out, stataus, subi_1_out, subi_2_out;

  Comparator #(.width(3), .mode("unsigned")) comparator_1 (.a(Op), .b(3'b111), .eq(comparator_1_eq));  // open: gt, lt
  Comparator #(.width(3), .mode("unsigned")) comparator_2 (
    .a(Op), .b(3'b000), .gt(comparator_2_gt), .eq(comparator_2_eq));  // open: lt
  Comparator #(.width(3)) comparator_3 (.a(Op), .b(3'b001), .eq(comparator_3_eq));  // open: gt, lt
  Comparator #(.width(3)) comparator_4 (.a(Op), .b(3'b010), .eq(comparator_4_eq));  // open: gt, lt
  Comparator #(.width(3)) comparator_5 (.a(Op), .b(3'b011), .eq(comparator_5_eq));  // open: gt, lt
  Comparator #(.width(3)) comparator_6 (.a(Op), .b(3'b100), .eq(comparator_6_eq));  // open: gt, lt
  Comparator #(.width(3)) comparator_7 (.a(Op), .b(3'b101), .eq(comparator_7_eq));  // open: gt, lt
  Comparator #(.width(3)) comparator_8 (.a(Op), .b(3'b110), .eq(comparator_8_eq));  // open: gt, lt
  Comparator #(.width(3)) comparator_9 (.a(Op), .b(3'b111), .eq(comparator_9_eq));  // open: gt, lt
  not not_1 (not_1_out, comparator_1_eq);
  not not_2 (not_2_out, Func);
  not not_3 (not_3_out, stataus);
  and and_1 (and_1_out, not_3_out, and_2_out);
  and and_2 (and_2_out, comparator_2_gt, not_1_out, not_2_out);
  and addi_1 (addi_1_out, comparator_3_eq, Func);
  and addi_2 (addi_2_out, comparator_3_eq, stataus);
  and subi_1 (subi_1_out, comparator_4_eq, Func);
  and subi_2 (subi_2_out, comparator_4_eq, stataus);
  and Beq_2 (Beq_2_out, comparator_5_eq, stataus);
  and Bnq_2 (Bnq_2_out, comparator_6_eq, stataus);
  and \tran  (ready, comparator_7_eq, stataus);
  and jmp (jmp_out, comparator_8_eq, stataus);
  D_Flip_Flop \_1表示当前已加载立即数  (.clk(clk), .D(and_1_out), .Q(stataus));  // open: Qn, preset, reset
  and and_3 (and_3_out, comparator_2_eq, Func);
  or or_1 (ALU_operation, and_3_out, subi_1_out, subi_2_out);
  or or_2 (update_inst, jmp_out, addi_1_out, comparator_2_eq, ready, addi_2_out, subi_2_out, Beq_2_out, Bnq_2_out, subi_1_out, comparator_9_eq);
  or or_3 (RegFile_we, comparator_2_eq, addi_1_out, addi_2_out, subi_1_out, subi_2_out);
  or or_4 (src_Y[1], addi_1_out, subi_1_out);
  or or_5 (src_Y[0], addi_2_out, addi_1_out, subi_1_out, subi_2_out);
  or or_6 (or_6_out, Beq_2_out, subi_1_out, Bnq_2_out);
  and and_4 (and_4_out, or_6_out, Equal);
  or or_7 (Pc_in, and_4_out, jmp_out);
  // Probe on stataus

  // Notes on the sheet:
  //   有限状态机
  //   节拍发生器
  //   硬布线控制电路
  //   ALU运算类型
  //   指令寄存器更新
  //   寄存器读写
  //   ALU操作数Y
  //   PC是否从输入端接收值
  //   data_sram信号是否有效
  //   输入输出总览
endmodule
